# Fritzing sketch final (saved by Fritzing 0.9.3b)
circuit board: 8.46667cm x 5.64444cm
breadboards: 1

parts:
  SW-1 = Vibration sensor module
  hc-sr1 = hc-sr04
  Part1 = KY-002 Vibration Switch Module [package="Breakout board"]
  Part3 = KY-012 Active Buzzer Module [package="Breakout board"]
  Part4 = Arduino Uno (Rev3) - ICSP

nets:
  VCC: SW-1.vcc, hc-sr1.VCC, Part1.Vin, Part3.S, Part4.5V, Part4.D3_PWM
  GND: SW-1.Ground, hc-sr1.GND, Part1.-, Part3.-, Part4.GND
  N1: SW-1.Digital_output, Part4.D11_PWM/MOSI
  N2: hc-sr1.Trig, Part4.D10_PWM/SS
  N3: hc-sr1.Echo, Part4.D9_PWM
  N4: Part1.S, Part4.D6_PWM

notes:
  SW-420 VIBRATION SENSOR
  HC-SR04 ULTRASONIC SENSOR
  YL-44 ACTIVE BUZZER
  KY031 SHOCK SENSOR
  ARDUINO UNO MICROCONTROLLER

custom parts:
  Vibration sensor module: Single-roller type full induction trigger switch. When no vibration or tilt, the product is ON conduction state, and in the steady state, when a vibration or tilt, the switch will be rendered instantly disconnect the conductive resistance increases, generating a current pulse signal, thereby triggering circuit. The default state of the swith is close Digital output Supply voltage:3.3V-5V On-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
  KY-002 Vibration Switch Module: Arduino Vibration Switch Module KY-002 Keyes allows detection of shock and vibration.
  KY-012 Active Buzzer Module: Active Piezoelectric Buzzer Module Keyes KY-012, it produces single-tone sound when signal is high.

// code stored in the sketch: final.ino

int const trigPin = 10;
int const echoPin = 9;
int buzzPin = 3;
int vibPin =11;
int shkPin = 6;
int shk;

void setup()

{
  pinMode(buzzPin, OUTPUT);
  pinMode(vibPin, INPUT);
	pinMode(shkPin, INPUT);
  pinMode(trigPin, OUTPUT); // trig pin will have pulses output
  pinMode(echoPin, INPUT); // echo pin should be input to get pulse width

  Serial.begin(9600); 
}



void loop()

{
  long measurement =vibration();
  delay(5);
 
  Serial.println(measurement);
  


	Serial.println(shkPin);
 delay(1); 
  if(digitalRead(shkPin)==LOW)
{
    Serial.println("Shock Detected");
    Serial.println("Resetting...");
		digitalWrite(buzzPin, LOW);
    delay(500); 
}
	else{
    digitalWrite(buzzPin, HIGH); 
  }  


  int duration, distance; 
 delay(1);
 digitalWrite(trigPin, HIGH);  
  delay(1);
  digitalWrite(trigPin, LOW);     // Measure the pulse input in echo pin

  duration = pulseIn(echoPin, HIGH);  // Distance is half the duration devided by 29.1 (from datasheet)
 
  distance = (duration/2) / 29.1;    // if distance less than 0.15 meter and more than 0 (0 or less means over range) 
 
    if (distance <= 7.5 && distance >= 0)  {
      // Buzz
      digitalWrite(buzzPin, LOW);
      Serial.println("Proximity ALert");
      Serial.println("Resetting...");
      
      
    }

    else if (measurement > 25000){
    digitalWrite(buzzPin, LOW);
    Serial.println("Strong Vibration Detected");
    Serial.println("Resetting...");
    delay(500);
  }
    else {
      // Don't buzz
      digitalWrite(buzzPin, HIGH);
     

    }
    // Waiting 60 ms won't hurt any one
    delay(1);

}
long vibration(){
  delay(10);
  long measurement=pulseIn (vibPin, HIGH);  //wait for the pin to get HIGH and returns measurement
  return measurement;
}
