# Fritzing sketch sketch (saved by Fritzing 0.9.3b)
breadboards: 1

parts:
  Part1 = Arduino Nano (Rev3.0)
  SW-2 = Vibration sensor module
  LED1 = LED - 3mm [color="Red (633nm)" package="3 mm [THT]"]
  R1 = Resistor [tolerance=±5% resistance=220 package="0603 [SMD]"]
  SW-1 = Vibration sensor module
  hc-sr1 = hc-sr04

nets:
  N1: Part1.D3, SW-2.Digital_output
  N2: Part1.D4, R1.Pin_1
  N3: Part1.D7, hc-sr1.Trig
  N4: Part1.D8, hc-sr1.Echo
  N5: Part1.D9, SW-1.Digital_output
  GND: Part1.GND, SW-2.Ground, LED1.cathode, SW-1.Ground, hc-sr1.GND
  VCC: Part1.5V, SW-2.vcc, SW-1.vcc, hc-sr1.VCC
  N6: LED1.anode, R1.Pin_0

notes:
  VIBRATION SENSOR
  SW-420
  SHOCK SENSOR
  KY-002
  ARDUINO NANO V3
  ULTRASONIC DISTANCE SENSOR
  HR-SR04

custom parts:
  Vibration sensor module: Single-roller type full induction trigger switch. When no vibration or tilt, the product is ON conduction state, and in the steady state, when a vibration or tilt, the switch will be rendered instantly disconnect the conductive resistance increases, generating a current pulse signal, thereby triggering circuit. The default state of the swith is close Digital output Supply voltage:3.3V-5V On-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

// code stored in the sketch: draft1.ino


int ledPin = 4;
int vibPin =9;
int shkPin = 3;
int shk;
const int pingPin = 7; // Trigger Pin of Ultrasonic Sensor
const int echoPin = 6; // Echo Pin of Ultrasonic Sensor



void setup()

{
  pinMode(ledPin, OUTPUT);
  pinMode(vibPin, INPUT);
	pinMode(shkPin, INPUT);

  Serial.begin(9600); 
}



void loop()

{
  long measurement =vibration();
  delay(50);
 
  Serial.println(measurement);
  if (measurement > 5000){
    digitalWrite(ledPin, HIGH);
  }
  else{
    digitalWrite(ledPin, LOW); 
  }


	
  delay(1); 
  if(digitalRead(shkPin)==LOW
{
    Serial.println("Shock Detected");
    Serial.println("Resetting...");
		digitalWrite(ledPin, HIGH);
    delay(500); 
}
	else{
    digitalWrite(ledPin, LOW); 
  }  



}

long vibration(){
  delay(10);
  long measurement=pulseIn (vibPin, HIGH);  //wait for the pin to get HIGH and returns measurement
  return measurement;
}
